# Fritzing sketch Hyrotracker (saved by Fritzing 0.9.3b)
circuit board: 8.46667cm x 5.64444cm
breadboards: 1

parts:
  LCD1 = LCD screen
  Part1 = Arduino Uno (Rev3)
  GY1 = MPU-6050 Board GY-521 [form="♀ (female)" package=THT]

nets:
  VSS: LCD1.VSS, LCD1.V0, LCD1.R/W, LCD1.LED-, Part1.GND, GY1.pin2
  N1: LCD1.RS, Part1.D4
  N2: LCD1.E, Part1.D5_PWM
  N3: LCD1.DB4, Part1.D10_PWM/SS
  N4: LCD1.DB5, Part1.D11_PWM/MOSI
  N5: LCD1.DB6, Part1.D12/MISO
  N6: LCD1.DB7, Part1.D13/SCK
  N7: LCD1.LED+, Part1.D3_PWM
  N8: Part1.A4/SDA, GY1.pin4
  N9: Part1.A5/SCL, GY1.pin3
  N10: Part1.D2, GY1.pin8
  N11: Part1.5V, GY1.pin1

custom parts:
  MPU-6050 Board GY-521: Acelerometro y Giroscopio MPU-6050 Board GY-521
